// Logisim project 2 bit logic unit.circ as structural Verilog: 1 circuit, main circuit main
module main (
  input  A0,
  input  B0,
  input  A1,
  input  B1,
  input  select_bit,
  output C1,
  output C2,
  output Cout
);

  wire adder_1_cout, adder_1_out, adder_2_out, and_1_out, and_2_out, not_1_out, not_2_out, or_1_out,
       or_2_out, xor_1_out, xor_2_out;

  and and_1 (and_1_out, A0, B0);
  or or_1 (or_1_out, A0, B0);
  xor xor_1 (xor_1_out, A0, B0);
  not not_1 (not_1_out, A0);
  and and_2 (and_2_out, A1, B1);
  or or_2 (or_2_out, A1, B1);
  xor xor_2 (xor_2_out, A1, B1);
  not not_2 (not_2_out, A1);
  Adder #(.width(1)) adder_1 (.a(xor_1_out), .b(not_1_out), .out(adder_1_out), .cin(select_bit), .cout(adder_1_cout));
  Adder #(.width(1)) adder_2 (.a(xor_2_out), .b(not_2_out), .out(adder_2_out), .cin(adder_1_cout), .cout(Cout));
  Multiplexer multiplexer_1 (.in0(and_1_out), .in1(adder_1_out), .out(C1), .sel(select_bit));  // open: en
  Multiplexer multiplexer_2 (.in0(and_2_out), .in1(adder_2_out), .out(C2), .sel(select_bit));  // open: en
endmodule
