// Logisim project first.circ as structural Verilog: 1 circuit, main circuit main
module main (
  input  in_1,
  input  in_2,
  input  in_3,
  input  in_4,
  input  in_5,
  input  in_6,
  output out_7,
  output out_8,
  output out_9,
  output out_10,
  output out_11,
  output out_12
);

  wire adder_1_p3, adder_1_p4, adder_1_p5, adder_2_p5, and_1_out, and_2_out, and_3_out, and_4_out,
       multiplexer_1_out, multiplexer_2_out, multiplexer_4_p3, not_1_out, not_2_out, not_3_out, or_1_out,
       or_2_out, or_3_out, xor_1_out, xor_2_out;

  xor xor_1 (xor_1_out, in_4, adder_1_p3);
  and and_1 (and_1_out, in_3, in_3, in_4);
  or or_1 (or_1_out, in_3, in_4);
  and and_2 (and_2_out, in_5, in_5, in_6);
  or or_2 (or_2_out, in_5, in_6);
  xor xor_2 (xor_2_out, in_6, adder_1_p3);
  // Adder adder_1: pin names not known; wires that end beside it: in_3, xor_1_out, adder_1_p3, adder_1_p4, adder_1_p5
  // Adder adder_2: pin names not known; wires that end beside it: in_5, xor_2_out, adder_1_p4, out_12, adder_2_p5
  Multiplexer multiplexer_1 (.in0(and_1_out), .in1(or_1_out), .out(multiplexer_1_out));  // open: sel, en
  Multiplexer multiplexer_2 (.in0(and_2_out), .in1(or_2_out), .out(multiplexer_2_out));  // open: sel, en
  not not_1 (not_1_out, in_5);
  Multiplexer multiplexer_3 (.in0(multiplexer_1_out), .in1(adder_1_p5), .out(out_7));  // open: sel, en
  // Multiplexer multiplexer_4: pin names not known; wires that end beside it: multiplexer_2_out, adder_2_p5, multiplexer_4_p3, out_8
  not not_2 (not_2_out, out_8);
  not not_3 (not_3_out, in_5);
  and and_3 (and_3_out, not_2_out, in_5, xor_2_out);
  and and_4 (and_4_out, not_3_out, out_8, not_1_out);
  or or_3 (or_3_out, out_8, out_8);
  not not_4 (out_9, or_3_out);
  or or_4 (out_11, and_3_out, and_4_out);

  assign out_10 = out_8;
endmodule
